# Fritzing sketch Final Project Fritzing (saved by Fritzing 0.7.12b)
breadboards: 1

parts:
  VCC1 = Battery block 9V
  Arduino1 = Arduino
  R1 = Photocell (LDR) [package=THT]
  R2 = 10k Ω Resistor [package=THT]
  R4 = Trimmer Potentiometer [package=THT]
  J2 = Piezo Speaker
  LED1 = LED - 3mm [color="Red (633nm)" package="3 mm [THT]"]
  LED2 = LED - 3mm [color="Red (633nm)" package="3 mm [THT]"]
  R5 = 330 Ω Resistor [package=THT]
  R6 = 330 Ω Resistor [package=THT]
  J3 = Basic Servo

nets:
  GND: VCC1.-, Arduino1.GND, R2.Pin_0, R4.leg1, J2.pin1, R5.Pin_0, R6.Pin_0, J3.gnd
  N1: VCC1.+, J3.vcc
  N2: Arduino1.D12, J2.pin2
  N3: Arduino1.D11, J3.pulse
  N4: Arduino1.D3, LED1.anode
  N5: Arduino1.D2, LED2.anode
  N6: Arduino1.+5V, R1.pin_1, R4.leg2
  N7: Arduino1.A0, R1.pin_0, R2.Pin_1
  N8: Arduino1.A1, R4.wiper
  N9: LED1.cathode, R5.Pin_1
  N10: LED2.cathode, R6.Pin_1

notes:
  The vex motor has three wires that are attached to a ground, signal, and current. It winds back to provide tension in the rubber band.
  The piezo produces sound for the launch sequence and the inititation phase. It acts as the key inidcator
  The photoresistor takes the value of the light at each moment and when it goes below 700, the motor will react by turning full throtle clockwise
  The two LED's indicate which part of the launch the device is in. If the pin 3 LED is on, then the launch has not yet begun. Once the pin 3 LED turns off and the pin 2 LED turns on, then the launch has begun.
  The potentiometer reads a value according to a clockwise or counterclockwise spin. We programmed this sensor to start the launch and wind back the rubber band when the potentionmeter reads a value less than 500.
  The Nine-volt battery provides power to the vex motor since the negative terminal is plugged into ground and the positive terminal is plugged into the positive rail.
  The arduino board provides inputs for the bread board to connect to. The ports and pin numbers all come from the arduino.
